// Logisim project Contador_Inteligente.circ as structural Verilog: 3 circuits, main circuit main
module main (
  input  in_1,
  input  in_2,
  input  in_3,
  input  in_4,
  input  in_5,
  input  in_6,
  input  in_7,
  input  in_8,
  input  in_9,
  input  in_10,
  input  in_11,
  input  in_12,
  input  in_13,
  input  in_14,
  output [3:0] LSB,
  output [3:0] MSB,
  output [3:0] DEZENAS,
  output [3:0] CENTENAS,
  output [3:0] out_19,
  output [3:0] DEZENAS_2
);

  // MX_MI mx_mi_1: pin names not known; wires that end beside it: in_8, in_10, out_19, {in_14, in_13, in_12, in_11}, DEZENAS, {in_9, in_7, in_6, in_5}, LSB, {in_4, in_3, in_2, in_1}, MSB, {in_14, in_13, in_12, in_11}, CENTENAS, {in_9, in_7, in_6, in_5}, DEZENAS_2, {in_4, in_3, in_2, in_1}

  // Other names for the same wires on the sheet: A0C = in_11; A1C = in_12; A2C = in_13; A3C = in_14; A0D = in_5;
  //   A1D = in_6; A2D = in_7; A3D = in_9; A0U = in_1; A1U = in_2; A2U = in_3; A3U = in_4

  // Notes on the sheet:
  //   UNIDADES
  //   DEZENAS
  //   CENTENAS
  //   CENTENAS
  //   MSB
  //   UNIDADES
  //   LSB
  //   UNIDADES
endmodule

module Armazenador_de_bits (
  input  in_1,
  input  in_2,
  input  in_3,
  input  in_4,
  input  in_5,
  input  in_6,
  input  in_7,
  input  in_8,
  input  in_9,
  input  in_10,
  input  in_11,
  input  in_12,
  input  in_13,
  input  in_14,
  output LSB,
  output LSB_2,
  output LSB_3,
  output out_18,
  output out_19,
  output out_20,
  output out_21,
  output out_22,
  output out_23,
  output out_24,
  output MSB,
  output MSB_2
);

  wire multiplexer_1_out, multiplexer_2_out, multiplexer_3_out, multiplexer_4_out, multiplexer_5_out,
       multiplexer_6_out, multiplexer_7_out, multiplexer_8_out, multiplexer_9_out, multiplexer_10_out,
       multiplexer_11_out, multiplexer_12_out;

  D_Flip_Flop d_ff_1 (.clk(in_13), .D(multiplexer_1_out), .Q(LSB));  // open: Qn, preset, en, reset
  Multiplexer #(.enable("false")) multiplexer_1 (.in0(LSB), .in1(in_1), .out(multiplexer_1_out), .sel(in_14));
  D_Flip_Flop d_ff_2 (.clk(in_13), .D(multiplexer_2_out), .Q(out_18));  // open: Qn, preset, en, reset
  Multiplexer #(.enable("false")) multiplexer_2 (.in0(out_18), .in1(in_4), .out(multiplexer_2_out), .sel(in_14));
  D_Flip_Flop d_ff_3 (.clk(in_13), .D(multiplexer_3_out), .Q(out_21));  // open: Qn, preset, en, reset
  Multiplexer #(.enable("false")) multiplexer_3 (.in0(out_21), .in1(in_7), .out(multiplexer_3_out), .sel(in_14));
  D_Flip_Flop d_ff_4 (.clk(in_13), .D(multiplexer_4_out), .Q(out_24));  // open: Qn, preset, en, reset
  Multiplexer #(.enable("false")) multiplexer_4 (.in0(out_24), .in1(in_10), .out(multiplexer_4_out), .sel(in_14));
  D_Flip_Flop d_ff_5 (.clk(in_13), .D(multiplexer_5_out), .Q(LSB_2));  // open: Qn, preset, en, reset
  Multiplexer #(.enable("false")) multiplexer_5 (.in0(LSB_2), .in1(in_2), .out(multiplexer_5_out), .sel(in_14));
  D_Flip_Flop d_ff_6 (.clk(in_13), .D(multiplexer_6_out), .Q(out_19));  // open: Qn, preset, en, reset
  Multiplexer #(.enable("false")) multiplexer_6 (.in0(out_19), .in1(in_5), .out(multiplexer_6_out), .sel(in_14));
  D_Flip_Flop d_ff_7 (.clk(in_13), .D(multiplexer_7_out), .Q(out_22));  // open: Qn, preset, en, reset
  Multiplexer #(.enable("false")) multiplexer_7 (.in0(out_22), .in1(in_8), .out(multiplexer_7_out), .sel(in_14));
  D_Flip_Flop d_ff_8 (.clk(in_13), .D(multiplexer_8_out), .Q(MSB));  // open: Qn, preset, en, reset
  Multiplexer #(.enable("false")) multiplexer_8 (.in0(MSB), .in1(in_11), .out(multiplexer_8_out), .sel(in_14));
  Multiplexer #(.enable("false")) multiplexer_9 (.in0(out_23), .in1(in_9), .out(multiplexer_9_out), .sel(in_14));
  Multiplexer #(.enable("false")) multiplexer_10 (.in0(MSB_2), .in1(in_12), .out(multiplexer_10_out), .sel(in_14));
  D_Flip_Flop d_ff_9 (.clk(in_13), .D(multiplexer_11_out), .Q(LSB_3));  // open: Qn, preset, en, reset
  Multiplexer #(.enable("false")) multiplexer_11 (.in0(LSB_3), .in1(in_3), .out(multiplexer_11_out), .sel(in_14));
  D_Flip_Flop d_ff_10 (.clk(in_13), .D(multiplexer_12_out), .Q(out_20));  // open: Qn, preset, en, reset
  Multiplexer #(.enable("false")) multiplexer_12 (.in0(out_20), .in1(in_6), .out(multiplexer_12_out), .sel(in_14));
  D_Flip_Flop d_ff_11 (.clk(in_13), .D(multiplexer_9_out), .Q(out_23));  // open: Qn, preset, en, reset
  D_Flip_Flop d_ff_12 (.clk(in_13), .D(multiplexer_10_out), .Q(MSB_2));  // open: Qn, preset, en, reset

  // Other names for the same wires on the sheet: CLK = in_13; LOAD = in_14

  // Notes on the sheet:
  //   A0
  //   ENTRADA DE CLK
  //   MSB
  //   ENTRADA DE LOAD
  //   A1
  //   A2
endmodule

module MX_MI (
  input  in_1,
  input  in_2,
  input  in_3,
  input  [3:0] DEZENAS,
  input  [3:0] DEZENAS_2,
  input  [3:0] in_6,
  input  [3:0] in_7,
  input  UNIDADES,
  input  in_9,
  input  in_10,
  input  in_11,
  input  in_12,
  input  in_13,
  input  in_14,
  input  in_15,
  output [3:0] UNIDADES_2,
  output [3:0] UNIDADES_3,
  output [3:0] DEZENAS_3,
  output [3:0] DEZENAS_4,
  output [3:0] out_20,
  output [3:0] out_21
);

  wire and_1_out, and_2_out, not_1_out;

  and and_1 (and_1_out, in_1, in_2);
  Armazenador_de_bits armazenador_de_bits_1 (
    .in_13(and_1_out), .in_14(in_3), .in_3(DEZENAS_2[0]), .LSB_3(out_21[0]), .out_20(out_21[1]),
    .in_6(DEZENAS_2[1]), .out_23(out_21[2]), .in_9(DEZENAS_2[2]), .MSB_2(out_21[3]), .in_12(DEZENAS_2[3]),
    .LSB(UNIDADES_3[0]), .in_1(in_14), .out_18(UNIDADES_3[1]), .in_4(in_12), .out_21(UNIDADES_3[2]),
    .out_24(UNIDADES_3[3]), .in_10(UNIDADES), .LSB_2(DEZENAS_4[0]), .in_2(in_7[0]), .out_19(DEZENAS_4[1]),
    .in_5(in_7[1]), .out_22(DEZENAS_4[2]), .in_8(in_7[2]), .MSB(DEZENAS_4[3]), .in_11(in_7[3]), .in_7(in_10));
  and and_2 (and_2_out, in_1, not_1_out);
  not not_1 (not_1_out, in_2);
  Armazenador_de_bits armazenador_de_bits_2 (
    .in_13(and_2_out), .in_14(in_3), .in_3(DEZENAS[0]), .LSB_3(out_20[0]), .out_20(out_20[1]),
    .in_6(DEZENAS[1]), .out_23(out_20[2]), .in_9(DEZENAS[2]), .MSB_2(out_20[3]), .in_12(DEZENAS[3]),
    .LSB(UNIDADES_2[0]), .in_1(in_15), .out_18(UNIDADES_2[1]), .in_4(in_13), .out_21(UNIDADES_2[2]),
    .out_24(UNIDADES_2[3]), .in_10(in_9), .LSB_2(DEZENAS_3[0]), .in_2(in_6[0]), .out_19(DEZENAS_3[1]),
    .in_5(in_6[1]), .out_22(DEZENAS_3[2]), .in_8(in_6[2]), .MSB(DEZENAS_3[3]), .in_11(in_6[3]), .in_7(in_11));

  // Other names for the same wires on the sheet: CLK = in_1; LOAD = in_3; MX_MI = in_2

  // Notes on the sheet:
  //   CENTENAS
  //   CENTENAS
  //   MÁXIMO
  //   CENTENAS
  //   CENTENAS
  //   MÍNIMO
  //   ENTRADA DE CLK
  //   ENTRADA MX_MI
  //   ENTRADA DE LOAD
endmodule
